# Fritzing sketch connection (saved by Fritzing 0.9.10b)

parts:
  M1 = Nucleo 144 MB1137
  A1 = Waveshare 1.54in epaper display

nets:
  N1: M1.+3.3V, A1.Pin_8
  N2: M1.GND, A1.Pin_7
  N3: M1.PA3, A1.Pin_3
  N4: M1.PA10, A1.Pin_4
  N5: M1.PB3, A1.Pin_5
  N6: M1.PB5, A1.Pin_6
  N7: M1.PB10, A1.Pin_2
  N8: M1.PC7, A1.Pin_1

notes:
  BUSY
  DC
  CLK
  RST
  CS
  DIN
  GND
  VCC

custom parts:
  Nucleo 144 MB1137: The STM32 Nucleo-144 boards based on the MB1137 reference board (NUCLEO-F207ZG, NUCLEO-F303ZE, NUCLEO-F412ZG, NUCLEO-F413ZH, NUCLEO-F429ZI, NUCLEO-F439ZI, NUCLEO-F446ZE, NUCLEO-F722ZE, NUCLEO-F746ZG, NUCLEO-F756ZG, NUCLEO-F767ZI and NUCLEO-H743ZI) provide an affordable and flexible way for users to try out new concepts and build prototypes with STM32 microcontrollers.
  Waveshare 1.54in epaper display: This is an E-Ink display module, 1.54inch, 200x200 resolution, with embedded controller, communicating via SPI interface.
